# Fritzing sketch a4988 (saved by Fritzing 0.9.3b)
breadboards: 1

parts:
  Pololu_A1 = Pololu A4988 [package=SO16]
  JACK1 = 2.1mm Barrel Jack with Terminal Block
  M1 = Stepper Motor - Bipolar
  Raspberry_Pi_1 = Raspberry Pi 3 [part_number=RPI-3-V1.2]

nets:
  N1: Pololu_A1.RESET, Pololu_A1.SLEEP
  N2: Pololu_A1.STEP, Raspberry_Pi_1.GIPO26
  N3: Pololu_A1.DIR, Raspberry_Pi_1.GIPO19
  GND: Pololu_A1.GND, JACK1.NEG, Raspberry_Pi_1.GND
  VDD: Pololu_A1.VDD, Raspberry_Pi_1.3v3
  N4: Pololu_A1.1B, M1.D
  N5: Pololu_A1.1A, M1.B
  N6: Pololu_A1.2A, M1.C
  N7: Pololu_A1.2B, M1.A
  N8: Pololu_A1.VMOT, JACK1.POS

notes:
  コイル1
  コイル2
  モーター用DC電源(モータスペックに依る）
  A4988
  ２相　バイポーラ　ステッピングモータ
  RESET
  SLEEP
  STEP
  DIR
  VMOT
  MOTOR GND
  LOGIC GND
  VDD
