# Fritzing sketch HBridge_L298N (saved by Fritzing 0.9.3b)

parts:
  Raspberry_Pi_1 = Raspberry Pi 3 [part_number=RPI-3-V1.2]
  S1 = H-Bridge with L298N
  M1 = DC Motor

nets:
  N1: Raspberry_Pi_1.GPIO21, S1.IN2
  N2: Raspberry_Pi_1.GPIO20, S1.IN1
  GND: Raspberry_Pi_1.GND, S1.GND
  5V: Raspberry_Pi_1.5V, S1.12V, S1.5V
  N3: S1.ENA, S1.ENA-5V
  N4: S1.M1-01, M1.pin_2
  N5: S1.M1-02, M1.pin_1

notes:
  5V DC Motor

custom parts:
  H-Bridge with L298N: h-bridge
