# Fritzing sketch HBridge_TA7291P (saved by Fritzing 0.9.3b)
breadboards: 1

parts:
  Raspberry_Pi_1 = Raspberry Pi 3 [part_number=RPI-3-V1.2]
  U1 = TA7291P [package=HSIP10-P-2.54(THT)]
  M2 = DC Motor
  MOTOR_Power = 2.1mm Barrel Jack with Terminal Block
  part = Ceramic Capacitor [capacitance=100nF package="100 mil [THT, multilayer]"]

nets:
  N1: Raspberry_Pi_1.GPIO21, U1.IN2
  N2: Raspberry_Pi_1.GPIO20, U1.IN1
  GND: Raspberry_Pi_1.GND, U1.GND, MOTOR_Power.NEG, part.0
  5V: Raspberry_Pi_1.5V, U1.Vcc, part.1
  N3: U1.OUT1, M2.pin_2
  N4: U1.Vref, U1.Vs, MOTOR_Power.POS
  N5: U1.OUT2, M2.pin_1

custom parts:
  TA7291P: The IC are Full-Bridge Driver. 4 modes available (CW / CCW / STOP / BRAKE) and PWM control. Output current:1.0 A (AVE.) 2.0 A (PEAK)
