# Fritzing sketch ADS1115_LoadCell (saved by Fritzing 0.9.3b)

parts:
  Raspberry_Pi_1 = Raspberry Pi 3 [part_number=RPI-3-V1.2]
  パーツ1 = Adafruit ADS1115 16Bit I2C ADC [part_number="Adafruit #1085"]
  LoadCell = Load Cell [chip_label=LoadCell package="SIP (Single Inline) [THT]"]

nets:
  3V3: Raspberry_Pi_1.3v3, パーツ1.VDD
  N1: Raspberry_Pi_1.GPIO2, パーツ1.SDA
  N2: Raspberry_Pi_1.GPIO3, パーツ1.SCL
  GND: Raspberry_Pi_1.GND, パーツ1.GND, LoadCell.pin3
  N3: Raspberry_Pi_1.5V, LoadCell.pin4
  N4: パーツ1.AIN1, LoadCell.pin2
  N5: パーツ1.AIN0, LoadCell.pin1

custom parts:
  Adafruit ADS1115 16Bit I2C ADC: For microcontrollers without an analog-to-digital converter or when you want a higher-precision ADC, the ADS1115 provides 16-bit precision at 860 samples/second over I2C. The chip can be configured as 4 single-ended input channels, or two differential channels. As a nice bonus, it even includes a programmable gain amplifier, up to x16, to help boost up smaller single/differential signals to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
  Load Cell: A SIP stand-in part for whatever you want. With 4 pins on a 300 mil single inline package (SIP) footprint.
