# Fritzing sketch APDS9960 (saved by Fritzing 0.9.3b)

parts:
  Raspberry_Pi_1 = Raspberry Pi 3 [part_number=RPI-3-V1.2]
  パーツ1 = Adafruit APDS-9960 [part_number="Adafruit #3595"]

nets:
  3V3: Raspberry_Pi_1.3v3, パーツ1.VIN
  N1: Raspberry_Pi_1.GPIO2, パーツ1.SDA
  N2: Raspberry_Pi_1.GPIO3, パーツ1.SCL
  GND: Raspberry_Pi_1.GND, パーツ1.GND

notes:
  VIN
  GND
  SCL
  SDA

custom parts:
  Adafruit APDS-9960: The APDS9960 from Avago Technologies has an integrated IR LED and driver, along with four directional photodiodes that sense reflected IR energy from the LED. It's proximity detection feature allows it to measure the distance an object is from the front of the sensor (up to a few centimeters) with 8 bit resolution. Since there are four IR sensors, you can measure the changes in light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
