# Fritzing sketch BH1750 (saved by Fritzing 0.9.3b)

parts:
  Raspberry_Pi_1 = Raspberry Pi 3 [part_number=RPI-3-V1.2]
  パーツ3 = BH1750

nets:
  3V3: Raspberry_Pi_1.3v3, パーツ3.VCC
  N1: Raspberry_Pi_1.GPIO2, パーツ3.SDA
  N2: Raspberry_Pi_1.GPIO3, パーツ3.SCL
  GND: Raspberry_Pi_1.GND, パーツ3.GND

custom parts:
  BH1750: Light Sensor
