# Fritzing sketch HT16K33 (saved by Fritzing 0.9.3b)
breadboards: 1

parts:
  MCU1 = Raspberry Pi Zero
  パーツ1 = Mini 8x8 LED Matrix Backpack [part_number=959]

nets:
  N1: MCU1.pin_1, MCU1.pin_17, パーツ1.VDD
  N2: MCU1.pin_3, パーツ1.SDA
  N3: MCU1.pin_5, パーツ1.SCL
  N4: MCU1.pin_6, パーツ1.GND

custom parts:
  Mini 8x8 LED Matrix Backpack: This 0.8" 8x8 monochrome LED matrix includes a driver chip for simple control via an I2C interface. The backpack features address-selection jumpers so you can connect up to four matrices on a single I2C bus.
