# Fritzing sketch HT16K33 (saved by Fritzing 0.9.3b)
perfboards: 1

parts:
  MCU1 = Raspberry Pi Zero  # not connected
  DI1 = 16-segment display [package=THT]
  DI2 = 16-segment display [package=THT]
  DI3 = 16-segment display [package=THT]
  DI4 = 16-segment display [package=THT]  # not connected

nets:
  N1: DI1.anodeG, DI2.anodeE
  N2: DI1.anodeB, DI2.anodeH
  N3: DI1.anodeM, DI2.anodeF
  N4: DI2.anodeG, DI3.anodeE
  N5: DI2.anodeB, DI3.anodeH
  N6: DI2.anodeM, DI3.anodeF
  N7: DI2.anodeK, DI3.anodeA2

notes:
  SCL
  SDA
  GND
  VDD
