# Fritzing sketch HT16K33 (saved by Fritzing 0.9.3b)
perfboards: 1

parts:
  MCU1 = Raspberry Pi Zero  # not connected
  Dot_Matrix6 = LED Dot Matrix 18mm (0.7 INCH)
  Dot_Matrix7 = LED Dot Matrix 18mm (0.7 INCH)
  Dot_Matrix8 = LED Dot Matrix 18mm (0.7 INCH)
  Dot_Matrix9 = LED Dot Matrix 18mm (0.7 INCH)
  Dot_Matrix10 = LED Dot Matrix 18mm (0.7 INCH)  # not connected
  Dot_Matrix11 = LED Dot Matrix 18mm (0.7 INCH)  # not connected
  Dot_Matrix12 = LED Dot Matrix 18mm (0.7 INCH)  # not connected
  Dot_Matrix13 = LED Dot Matrix 18mm (0.7 INCH)  # not connected

nets:
  N1: Dot_Matrix6.Row_3, Dot_Matrix8.Column_1
  N2: Dot_Matrix6.Column_2, Dot_Matrix8.Row_3
  N3: Dot_Matrix6.Row_5, Dot_Matrix8.Column_2
  N4: Dot_Matrix6.Row_6, Dot_Matrix8.Row_5
  N5: Dot_Matrix6.Row_7, Dot_Matrix8.Row_6
  N6: Dot_Matrix6.Column_4, Dot_Matrix7.Row_7, Dot_Matrix8.Column_5, Dot_Matrix9.Row_6
  N7: Dot_Matrix6.Column_5, Dot_Matrix7.Row_6, Dot_Matrix8.Row_4, Dot_Matrix9.Row_5
  N8: Dot_Matrix6.Row_4, Dot_Matrix7.Row_5, Dot_Matrix8.Column_3, Dot_Matrix9.Column_2
  N9: Dot_Matrix6.Column_3, Dot_Matrix7.Column_2, Dot_Matrix8.Row_2, Dot_Matrix9.Row_3
  N10: Dot_Matrix6.Row_2, Dot_Matrix7.Row_3, Dot_Matrix8.Row_1, Dot_Matrix9.Column_1
  N11: Dot_Matrix6.Row_1, Dot_Matrix7.Column_1
  N12: Dot_Matrix7.Column_4, Dot_Matrix9.Column_5
  N13: Dot_Matrix7.Column_5, Dot_Matrix9.Row_4
  N14: Dot_Matrix7.Row_4, Dot_Matrix9.Column_3
  N15: Dot_Matrix7.Column_3, Dot_Matrix9.Row_2
  N16: Dot_Matrix7.Row_2, Dot_Matrix9.Row_1
  N17: Dot_Matrix8.Column_4, Dot_Matrix9.Row_7

notes:
  SCL
  SDA
  GND
  VDD
