# Fritzing sketch INA219 (saved by Fritzing 0.9.3b)

parts:
  Raspberry_Pi_1 = Raspberry Pi 3 [part_number=RPI-3-V1.2]
  パーツ1 = INA219 High Side DC Current Sensor Breakout [part_number=904]
  M1 = CHIBI Geared Motor [package="SIP (Single Inline) [THT]"]
  VCC1 = Battery

nets:
  3V3: Raspberry_Pi_1.3v3, パーツ1.VCC
  N1: Raspberry_Pi_1.GPIO2, パーツ1.SDA
  N2: Raspberry_Pi_1.GPIO3, パーツ1.SCL
  GND: Raspberry_Pi_1.GND, パーツ1.GND, M1.pin1, VCC1.-
  N3: パーツ1.VIN-, M1.pin2
  N4: パーツ1.VIN+, VCC1.+

notes:
  VCC
  GND
  SCL
  SDA
  Vin-
  Vin+

custom parts:
  INA219 High Side DC Current Sensor Breakout: This breakout board will solve all your power-monitoring problems. Instead of struggling with two multimeters, you can just use the handy INA219B chip on this breakout to both measure both the high side voltage and DC current draw over I2C with 1% precision. Most current-measuring devices such as our current panel meter are only good for low side measuring. That means that unless you want to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
  CHIBI Geared Motor: Micro Geared Motor
