# Fritzing sketch MLX90614 (saved by Fritzing 0.9.3b)

parts:
  Raspberry_Pi_1 = Raspberry Pi 3 [part_number=RPI-3-V1.2]
  MLX90614 = MLX90614 [package="SIP (Single Inline) [THT]"]

nets:
  N1: Raspberry_Pi_1.3v3, MLX90614.pin1
  N2: Raspberry_Pi_1.GPIO2, MLX90614.pin4
  N3: Raspberry_Pi_1.GPIO3, MLX90614.pin3
  N4: Raspberry_Pi_1.GND, MLX90614.pin2

notes:
  VIN
  GND
  SCL
  SDA

custom parts:
  MLX90614: MLX90614 breakout
