# Fritzing sketch TCS34725 (saved by Fritzing 0.9.3b)

parts:
  Raspberry_Pi_1 = Raspberry Pi 3 [part_number=RPI-3-V1.2]
  Part2 = Adafruit TCS34725 RGB Color Sensor [part_number="Adafruit #1334"]

nets:
  3V3: Raspberry_Pi_1.3v3, Part2.VIN
  N1: Raspberry_Pi_1.GPIO2, Part2.SDA
  N2: Raspberry_Pi_1.GPIO3, Part2.SCL
  GND: Raspberry_Pi_1.GND, Part2.GND

custom parts:
  Adafruit TCS34725 RGB Color Sensor: Your electronics can now see in dazzling color with this lovely color light sensor. We found the best color sensor on the market, the TCS34725, which has RGB and Clear light sensing elements. An IR blocking filter, integrated on-chip and localized to the color sensing photodiodes, minimizes the IR spectral component of the incoming light and allows color measurements to be made accurately. The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
