# Fritzing sketch VL53L1X (saved by Fritzing 0.9.3b)

parts:
  Raspberry_Pi_1 = Raspberry Pi 3 [part_number=RPI-3-V1.2]
  VL53L1X = VL53L1X [package="SIP (Single Inline) [THT]"]

nets:
  N1: Raspberry_Pi_1.3v3, VL53L1X.pin1
  N2: Raspberry_Pi_1.GPIO2, VL53L1X.pin2
  N3: Raspberry_Pi_1.GPIO3, VL53L1X.pin3
  N4: Raspberry_Pi_1.GND, VL53L1X.pin4

notes:
  VCC
  GND
  SCL
  SDA

custom parts:
  VL53L1X: VL53L1X breakout
