# Fritzing sketch seesaw (saved by Fritzing 0.9.3b)
breadboards: 1

parts:
  Raspberry_Pi_1 = Raspberry Pi 3 [part_number=RPI-3-V1.2]
  パーツ2 = Adafruit ATSAMD09D14 Breakout
  LED4 = LED - 3mm [color="Red (633nm)" package="3 mm [THT]"]
  S1 = Pushbutton [package=THT]
  S2 = Pushbutton [package=THT]
  S3 = Pushbutton [package=THT]
  R1 = TRIMPOT [package=trimpot_pth_s3_lock]
  LED5 = LED - 3mm [color="Red (633nm)" package="3 mm [THT]"]
  LED6 = LED - 3mm [color="Red (633nm)" package="3 mm [THT]"]
  LED7 = LED - 3mm [color="Red (633nm)" package="3 mm [THT]"]
  LED8 = LED - 3mm [color="Red (633nm)" package="3 mm [THT]"]
  R2 = Resistor [tolerance=±5% resistance=470 package="2010 [SMD]"]
  R3 = Resistor [tolerance=±5% resistance=470 package="2010 [SMD]"]
  R4 = Resistor [tolerance=±5% resistance=470 package="2010 [SMD]"]
  R5 = Resistor [tolerance=±5% resistance=470 package="2010 [SMD]"]
  R6 = Resistor [tolerance=±5% resistance=470 package="2010 [SMD]"]

nets:
  3V3: Raspberry_Pi_1.3v3, Raspberry_Pi_1.3V3, パーツ2.+5V, R1.CCW
  N1: Raspberry_Pi_1.GPIO2, パーツ2.PA22, パーツ2.PA04
  N2: Raspberry_Pi_1.GPIO3, パーツ2.PA23
  GND: Raspberry_Pi_1.GND, パーツ2.GND, LED4.cathode, S1.leg0, S2.leg0, S3.leg0, R1.CW, LED5.cathode, LED6.cathode, LED7.cathode, LED8.cathode
  N3: パーツ2.PA25, S1.leg1
  N4: パーツ2.PA24, S3.leg1
  N5: パーツ2.PA05, R1.WIPER
  N6: パーツ2.PA06, R2.Pin_0
  N7: パーツ2.PA09, S2.leg1
  N8: パーツ2.PA10, R6.Pin_0
  N9: パーツ2.PA11, R5.Pin_0
  N10: パーツ2.PA14, R4.Pin_0
  N11: パーツ2.PA15, R3.Pin_0
  N12: LED4.anode, R5.Pin_1
  N13: LED5.anode, R6.Pin_1
  N14: LED6.anode, R4.Pin_1
  N15: LED7.anode, R3.Pin_1
  N16: LED8.anode, R2.Pin_1

notes:
  VIN
  GND
  SCL
  SDA
  3.3V
  10KΩ
  470Ω
