# Fritzing sketch seesawNpix (saved by Fritzing 0.9.3b)

parts:
  Raspberry_Pi_1 = Raspberry Pi 3 [part_number=RPI-3-V1.2]
  パーツ2 = Adafruit ATSAMD09D14 Breakout
  NEOPIXEL1 = Neopixel 8x8 Matrix
  NEOPIXEL2 = Neopixel 8x8 Matrix

nets:
  3V3: Raspberry_Pi_1.3v3, パーツ2.+5V
  N1: Raspberry_Pi_1.GPIO2, パーツ2.PA22, パーツ2.PA04
  N2: Raspberry_Pi_1.GPIO3, パーツ2.PA23
  GND: Raspberry_Pi_1.GND, パーツ2.GND, NEOPIXEL1.GND, NEOPIXEL2.GND
  N3: Raspberry_Pi_1.5V, NEOPIXEL1.DIN, NEOPIXEL2.DIN
  N4: パーツ2.PA14, NEOPIXEL2.VCC
  N5: パーツ2.PA15, NEOPIXEL1.VCC

notes:
  VIN
  GND
  SCL
  SDA
  3.3V
  5V

custom parts:
  Neopixel 8x8 Matrix: Adafruit Neopixel 8x8 Matrix
