# Fritzing sketch schematic (saved by Fritzing 0.9.3b)

parts:
  Raspberry_Pi_1 = Raspberry Pi 3 [part_number=RPI-3-V1.2]
  U2 = SHT30 breakout [package="SIP (Single Inline) [THT]"]

nets:
  N1: Raspberry_Pi_1.3v3, U2.pin1
  N2: Raspberry_Pi_1.GPIO2, U2.pin4
  N3: Raspberry_Pi_1.GPIO3, U2.pin3
  N4: Raspberry_Pi_1.GND, U2.pin2

custom parts:
  SHT30 breakout: SHT30 Temperature Humidity sensor
