# Fritzing sketch SSD1306 (saved by Fritzing 0.9.3b)

parts:
  Raspberry_Pi_1 = Raspberry Pi 3 [part_number=RPI-3-V1.2]
  o1 = Module display OLED I2C 128x64 SSD1306 [package=THT]

nets:
  3V3: Raspberry_Pi_1.3v3, o1.VCC
  N1: Raspberry_Pi_1.GPIO2, o1.SDA
  N2: Raspberry_Pi_1.GPIO3, o1.SCL
  GND: Raspberry_Pi_1.GND, o1.GND

custom parts:
  Module display OLED I2C 128x64 SSD1306: Ecran OLED I2C SSD163 de 128x64 avec connexion I2C
