# Fritzing sketch stepping (saved by Fritzing 0.9.3b)

parts:
  パーツ2 = EasyDriver_v44
  M1 = Stepper Motor - Bipolar
  J1 = Power Jack [package=power_jack_pth_lock]
  Raspberry_Pi_1 = Raspberry Pi 3 [part_number=RPI-3-V1.2]
  パーツ6 = Arduino Uno (Rev3)
  U1 = FXMA2102 [chip_label=U package="DIP (Dual Inline) [THT]"]

nets:
  GND: パーツ2.GND, J1.GND, Raspberry_Pi_1.GND, パーツ6.GND, U1.GND
  N1: パーツ2.V+, J1.PWR
  N2: パーツ2.STEP, パーツ6.D8
  N3: パーツ2.DIR, パーツ6.D9_PWM
  N4: パーツ2.OUT2A, M1.A
  N5: パーツ2.OUT2B, M1.C
  N6: パーツ2.OUT1A, M1.B
  N7: パーツ2.OUT1B, M1.D
  N8: パーツ2.RESET, パーツ6.D10_PWM/SS
  N9: Raspberry_Pi_1.3v3, U1.VCCA, U1.OE
  N10: Raspberry_Pi_1.GPIO2, U1.A0
  N11: Raspberry_Pi_1.GPIO3, U1.A1
  5V: Raspberry_Pi_1.5V, パーツ6.5V, U1.VCCB
  N12: パーツ6.A4/SDA, U1.B0
  N13: パーツ6.A5/SCL, U1.B1

notes:
  ACアダプタから12Vを供給
  Arduino UNO
  Raspberry Pi 3 Model B
  Easy Driver V4.4
  バイポーラ　12V ステッピングモータ
  AE-FXMA2102
  I2C電圧レベル変換モジュール
  Arduinoの電源はRaspberry Pi から供給

custom parts:
  FXMA2102: I2C Bus Level Converter
